# Fritzing sketch project-scheme (saved by Fritzing 1.0.6)

parts:
  A1 = ESP32-S3 Terminal Adapter
  M1 = ESP32-S3-DevKitC-1-N8R8-v1 [part_number=ESP32-S3-DevKitC-1-N8R8-v1]
  R1 = Basic Flex Resistor [mn=1]
  R2 = Basic Flex Resistor [mn=1]
  R3 = Basic Flex Resistor [mn=1]
  R4 = Basic Flex Resistor [mn=1]
  R5 = Basic Flex Resistor [mn=1]
  R6 = Resistor [tolerance=±5% resistance=47k package="0805 [SMD]"]
  R7 = Resistor [tolerance=±5% resistance=47k package="0805 [SMD]"]
  R8 = Resistor [tolerance=±5% resistance=47k package="0805 [SMD]"]
  R9 = Resistor [tolerance=±5% resistance=47k package="0805 [SMD]"]
  R10 = Resistor [tolerance=±5% resistance=47k package="0805 [SMD]"]
  Grove1 = Grove OLED 128x96
  Part1 = InvenSense MPU6050

nets:
  VCC: A1.Pin_1, A1.Pin_2, A1.Pin_20, A1.Pin_21, A1.Pin_39, A1.Pin_40, M1.pin_1, M1.pin_2, R1.Pin_2, R2.pin_1, R3.Pin_2, R4.Pin_2, R5.Pin_2, Grove1.VCC, Part1.VCC
  N1: A1.Pin_3, A1.Pin_41, M1.pin_3
  N2: A1.Pin_4, A1.Pin_42, M1.pin_4
  N3: A1.Pin_5, A1.Pin_43, M1.pin_5, Grove1.SCL
  N4: A1.Pin_6, A1.Pin_44, M1.pin_6, Grove1.SDA
  N5: A1.Pin_7, A1.Pin_45, M1.pin_7
  N6: A1.Pin_8, A1.Pin_46, M1.pin_8
  N7: A1.Pin_9, A1.Pin_47, M1.pin_9
  N8: A1.Pin_10, A1.Pin_48, M1.pin_10
  N9: A1.Pin_11, A1.Pin_49, M1.pin_11
  N10: A1.Pin_12, A1.Pin_50, M1.pin_12
  N11: A1.Pin_13, A1.Pin_51, M1.pin_13, R3.pin_1
  N12: A1.Pin_14, A1.Pin_52, M1.pin_14
  N13: A1.Pin_15, A1.Pin_53, M1.pin_15, R4.pin_1
  N14: A1.Pin_16, A1.Pin_54, M1.pin_16, R5.pin_1
  N15: A1.Pin_17, A1.Pin_55, M1.pin_17
  N16: A1.Pin_18, A1.Pin_56, M1.pin_18
  N17: A1.Pin_19, A1.Pin_57, M1.pin_19
  N18: A1.Pin_58, A1.Pin_96, M1.pin_26
  N19: A1.Pin_59, A1.Pin_97, M1.pin_27
  N20: A1.Pin_60, A1.Pin_98, M1.pin_28
  N21: A1.Pin_61, A1.Pin_99, M1.pin_29
  N22: A1.Pin_62, A1.Pin_100, M1.pin_30
  N23: A1.Pin_63, A1.Pin_101, M1.pin_31
  N24: A1.Pin_64, A1.Pin_102, M1.pin_32
  N25: A1.Pin_65, A1.Pin_103, M1.pin_33, Part1.SDA
  N26: A1.Pin_66, A1.Pin_104, M1.pin_34, Part1.SCL
  N27: A1.Pin_67, A1.Pin_105, M1.pin_35
  N28: A1.Pin_68, A1.Pin_106, M1.pin_36
  N29: A1.Pin_69, A1.Pin_107, M1.pin_37
  N30: A1.Pin_70, A1.Pin_108, M1.pin_38
  N31: A1.Pin_71, A1.Pin_109, M1.pin_39
  N32: A1.Pin_72, A1.Pin_110, M1.pin_40, R1.pin_1
  N33: A1.Pin_73, A1.Pin_111, M1.pin_41, R2.Pin_2
  N34: A1.Pin_74, A1.Pin_112, M1.pin_42
  N35: A1.Pin_75, A1.Pin_113, M1.pin_43
  GND: A1.Pin_76, A1.Pin_95, A1.Pin_114, A1.pin_120, A1.pin_129, A1.pin_131, A1.pin_132, M1.pin_22, M1.pin_23, M1.pin_24, M1.pin_44, R6.Pin_1, R7.Pin_1, R8.Pin_1, R9.Pin_0, R10.Pin_0, Grove1.GND, Part1.GND
  N36: A1.pin_127, M1.pin_20
  N37: A1.pin_128, M1.pin_21
  N38: A1.pin_130, M1.pin_25

custom parts:
  ESP32-S3 Terminal Adapter: ESP32-S3 Terminal adapter 44 pin.
  ESP32-S3-DevKitC-1-N8R8-v1: ESP32-S3-DevKitC-1-N8R8-v1 This module is 44pins long (2x22) and 11 pins width.
